// Logisim project NSU-2023-T04L1e11.circ as structural Verilog: 1 circuit, main circuit mycircuit
module mycircuit (
  input  A,
  input  B,
  input  C,
  output R
);

  wire and_1_out, and_2_out, not_1_out, not_2_out;

  not not_1 (not_1_out, A);
  not not_2 (not_2_out, B);
  and and_1 (and_1_out, B, not_1_out);
  or or_1 (R, and_1_out, and_2_out);
  and and_2 (and_2_out, not_2_out, A);
endmodule
