// Logisim project NSU-2023-T04L1e17.circ as structural Verilog: 1 circuit, main circuit mycircuit
module mycircuit (
  input  A,
  input  B,
  input  C,
  output R
);

  wire not_1_out, or_1_out, or_2_out;

  or or_1 (or_1_out, A, B);
  or or_2 (or_2_out, C, not_1_out);
  not not_1 (not_1_out, A);
  and and_1 (R, or_1_out, or_2_out);
endmodule
