// Logisim project NSU-2023-T04L1e02.circ as structural Verilog: 1 circuit, main circuit mycircuit
module mycircuit (
  input  A,
  input  B,
  input  C,
  output R
);

  wire and_1_out, not_1_out, or_1_out;

  or or_1 (or_1_out, A, B);
  and and_1 (and_1_out, A, B);
  not not_1 (not_1_out, and_1_out);
  and and_2 (R, or_1_out, not_1_out);
endmodule
