// Logisim project NSU-2023-T05L1e11.circ as structural Verilog: 4 circuits, main circuit main
module main (
  input  [7:0] u,
  input  [7:0] v,
  output [7:0] R
);

  wire not_17_out;
  wire [7:0] add_1_sum, add_2_sum, add_4_sum, add_5_sum, inc_2_r, inc_3_r, mux_2_output, not_1_out, not_9_out;

  inc inc_1 ();  // open: X, R, Cout
  // Probe on u
  // Probe on v
  not not_1 (not_1_out[0], u[0]);
  not not_2 (not_1_out[1], u[1]);
  not not_3 (not_1_out[2], u[2]);
  not not_4 (not_1_out[3], u[3]);
  not not_5 (not_1_out[4], u[4]);
  not not_6 (not_1_out[5], u[5]);
  not not_7 (not_1_out[6], u[6]);
  not not_8 (not_1_out[7], u[7]);
  not not_9 (not_9_out[0], v[0]);
  not not_10 (not_9_out[1], v[1]);
  not not_11 (not_9_out[2], v[2]);
  not not_12 (not_9_out[3], v[3]);
  not not_13 (not_9_out[4], v[4]);
  not not_14 (not_9_out[5], v[5]);
  not not_15 (not_9_out[6], v[6]);
  not not_16 (not_9_out[7], v[7]);
  MUX mux_1 ();  // open: Input_0, sel, Input_1, Output
  inc inc_2 (.X(not_1_out), .R(inc_2_r));  // open: Cout
  inc inc_3 (.X(not_9_out), .R(inc_3_r));  // open: Cout
  // Probe on add_1_sum
  add add_1 (.A(8'h7), .B(inc_2_r), .sum(add_1_sum));  // open: Cout, Cin
  // Probe on add_2_sum
  add add_2 (.A(8'h7), .B(inc_3_r), .sum(add_2_sum));  // open: Cout, Cin
  add add_3 ();  // open: A, B, sum, Cout, Cin
  add add_4 (.A(8'h78), .B(u), .sum(add_4_sum));  // open: Cout, Cin
  add add_5 (.A(8'h78), .B(v), .sum(add_5_sum));  // open: Cout, Cin
  not not_17 (not_17_out, not_17_out);
  MUX mux_2 (.Input_0(add_5_sum), .sel(add_2_sum[7]), .Input_1(8'h78), .Output(mux_2_output));
  // NOT_Gate not_18 is placed but not wired
  MUX mux_3 (.Input_0(add_4_sum), .sel(add_1_sum[7]), .Input_1(mux_2_output), .Output(R));
  // OR_Gate or_1 is placed but not wired
  // OR_Gate or_2 is placed but not wired
  // Probe on R
  // AND_Gate and_1 is placed but not wired
  // AND_Gate and_2 is placed but not wired
  // XOR_Gate xor_1 is placed but not wired
  // XOR_Gate xor_2 is placed but not wired
  // XNOR_Gate xnor_1 is placed but not wired

  // Notes on the sheet:
  //   signed decimal:
  //   BOTH INPUTS use 2's comp
  //   signed decimal:
  //   split a bunch into 8 individual wires
  //   all the above are 8-bit devices
  //   You are only allowed to use Wiring and Gates libraries
  //   Chips you may use in addition to gates (Click and Ctrl/D duplicates):
  //   You may also use the following (and any other)  splitters facing any direction
  //   ATTENTION! DO NOT MOVE ANY PINS!
  //   Ignore overflow, unless instructed otherwise
  //   You may build and use your own chips using gates and wires
  //   out = A if sel=0
  //   B if sel=1
  //   extract the sign bit (bit 7) from an 8-bit bunch
  //   extract the LSB  (bit 0) from an 8-bit bunch
  //   constant 8-bit value (change it to anything  you want)
  //   Cin pulled to 0 if disconnected
  //   signed decimal:
  //   Gates: Click and Ctrl/D duplicates
  //   You may use any gates, not just the above ones
endmodule

module inc (
  input  [7:0] X,
  output [7:0] R,
  output Cout
);

  wire [7:1] and_1_out;

  assign {Cout, and_1_out} = {and_1_out, 1'b1} & X;  // AND_Gate and_1, 8 bits wide
  assign R = X ^ {and_1_out, 1'b1};  // XOR_Gate xor_1, 8 bits wide
endmodule

module add (
  input  [7:0] A,
  input  [7:0] B,
  input  Cin,
  output [7:0] sum,
  output Cout
);

  wire [6:0] or_1_out;
  wire [7:0] and_1_out, and_2_out, and_3_out;

  Pull_Resistor pull_resistor_1 (.node(Cin));
  assign and_1_out = A & B;  // AND_Gate and_1, 8 bits wide
  assign and_2_out = B & {or_1_out, Cin};  // AND_Gate and_2, 8 bits wide
  assign and_3_out = A & {or_1_out, Cin};  // AND_Gate and_3, 8 bits wide
  assign {Cout, or_1_out} = and_1_out | and_2_out | and_3_out;  // OR_Gate or_1, 8 bits wide
  assign sum = A ^ {or_1_out, Cin} ^ B;  // XOR_Gate xor_1, 8 bits wide
endmodule

module MUX (
  input  [7:0] Input_0,
  input  sel,
  input  [7:0] Input_1,
  output [7:0] Output
);

  wire [7:0] and_1_out, and_2_out;
  wire [7:7] not_1_out;

  not not_1 (not_1_out[7], sel);
  assign and_1_out = Input_0 & {8{not_1_out[7]}};  // AND_Gate and_1, 8 bits wide
  assign and_2_out = {8{sel}} & Input_1;  // AND_Gate and_2, 8 bits wide
  assign Output = and_1_out | and_2_out;  // OR_Gate or_1, 8 bits wide
endmodule
