// Logisim project 8-bit-adder.circ as structural Verilog: 1 circuit, main circuit dec
module dec (
  input  [7:0] X,
  input  [7:0] X_2,
  output [7:0] R,
  output [7:0] R_2,
  output Cout
);

  wire and_1_out, and_2_out, and_3_out, and_4_out, and_5_out, and_6_out, and_7_out, and_8_out, and_9_out,
       and_10_out, and_11_out, and_12_out, and_13_out, and_14_out, and_15_out, and_16_out, Cout_2_out,
       Cout_3_out, Cout_4_out, Cout_5_out, Cout_6_out, Cout_7_out, Cout_out, xor_1_out, xor_2_out, xor_3_out,
       xor_4_out, xor_5_out, xor_6_out, xor_7_out, xor_8_out;
  wire [7:0] xor_9_out;

  // Probe on X_2
  xor xor_1 (xor_1_out, X_2[0], 1'b1);
  and and_1 (and_1_out, X_2[0], 1'b1);
  xor xor_2 (xor_2_out, X_2[1], 1'b1);
  and and_2 (and_2_out, X_2[1], 1'b1);
  xor xor_3 (xor_3_out, X_2[2], 1'b1);
  and and_3 (and_3_out, X_2[2], 1'b1);
  xor xor_4 (xor_4_out, X_2[3], 1'b1);
  and and_4 (and_4_out, X_2[3], 1'b1);
  xor xor_5 (xor_5_out, X_2[4], 1'b1);
  and and_5 (and_5_out, X_2[4], 1'b1);
  xor xor_6 (xor_6_out, X_2[5], 1'b1);
  and and_6 (and_6_out, X_2[5], 1'b1);
  xor xor_7 (xor_7_out, X_2[6], 1'b1);
  and and_7 (and_7_out, X_2[6], 1'b1);
  xor xor_8 (xor_8_out, X_2[7], 1'b1);
  and and_8 (and_8_out, X_2[7], 1'b1);
  xor S (R_2[0], xor_1_out, 1'b0);
  and and_9 (and_9_out, xor_1_out, 1'b0);
  xor S_2 (R_2[1], xor_2_out, Cout_out);
  and and_10 (and_10_out, xor_2_out, Cout_out);
  xor S_3 (R_2[2], xor_3_out, Cout_2_out);
  and and_11 (and_11_out, xor_3_out, Cout_2_out);
  xor S_4 (R_2[3], xor_4_out, Cout_3_out);
  and and_12 (and_12_out, xor_4_out, Cout_3_out);
  xor S_5 (R_2[4], xor_5_out, Cout_4_out);
  and and_13 (and_13_out, xor_5_out, Cout_4_out);
  xor S_6 (R_2[5], xor_6_out, Cout_5_out);
  and and_14 (and_14_out, xor_6_out, Cout_5_out);
  xor S_7 (R_2[6], xor_7_out, Cout_6_out);
  and and_15 (and_15_out, xor_7_out, Cout_6_out);
  xor S_8 (R_2[7], xor_8_out, Cout_7_out);
  and and_16 (and_16_out, xor_8_out, Cout_7_out);
  or u_Cout (Cout_out, and_9_out, and_1_out);
  or Cout_2 (Cout_2_out, and_10_out, and_2_out);
  or Cout_3 (Cout_3_out, and_11_out, and_3_out);
  or Cout_4 (Cout_4_out, and_12_out, and_4_out);
  or Cout_5 (Cout_5_out, and_13_out, and_5_out);
  or Cout_6 (Cout_6_out, and_14_out, and_6_out);
  or Cout_7 (Cout_7_out, and_15_out, and_7_out);
  or Cout_8 (Cout, and_16_out, and_8_out);
  // Probe on R_2
  // Probe on X
  // Probe on X
  // Probe on {8{1'b1}}
  // Probe on {8{1'b1}}
  assign xor_9_out = X ^ {8{1'b1}};  // XOR_Gate xor_9, 8 bits wide
  // Probe on xor_9_out
  // Probe on xor_9_out
  assign R = X ^ xor_9_out;  // XOR_Gate xor_10, 8 bits wide
  // Probe on R
endmodule
