// Logisim project NSU-2023-T05L2e03.circ as structural Verilog: 2 circuits, main circuit formula
module formula (
  input  [7:0] A,
  output [7:0] R,
  output OFL
);

  wire [7:0] adder_1_r, adder_2_r, not_1_out;

  // Probe on A
  assign not_1_out = ~A;  // NOT_Gate not_1, 8 bits wide
  adder adder_1 (.A(not_1_out), .B(8'h1), .R(adder_1_r));
  adder adder_2 (.A(adder_1_r), .B(8'h33), .R(adder_2_r));
  or or_1 (OFL, adder_2_r[7], A[7]);
  // Probe on A
  // Probe on A
  adder adder_3 (.A(A), .B({A[5:0], 2'b00}), .R(R));
  // Probe on {A[5:0], 2'b00}
  // Probe on {A[5:0], 2'b00}
  // Probe on R
endmodule

module adder (
  input  [7:0] A,
  input  [7:0] B,
  output [7:0] R
);

  wire [7:0] and_1_out, and_2_out, and_3_out;
  wire [7:1] xor_1_out;
  wire [7:7] xor_1_out_2;

  assign and_1_out = B & A;  // AND_Gate and_1, 8 bits wide
  assign and_2_out = B & {xor_1_out, 1'b0};  // AND_Gate and_2, 8 bits wide
  assign and_3_out = A & {xor_1_out, 1'b0};  // AND_Gate and_3, 8 bits wide
  assign {xor_1_out_2[7], xor_1_out} = and_2_out ^ and_3_out ^ and_1_out;  // XOR_Gate xor_1, 8 bits wide
  assign R = A ^ B ^ {xor_1_out, 1'b0};  // XOR_Gate xor_2, 8 bits wide
endmodule
