// Logisim project NSU-2023-T05L2e04.circ as structural Verilog: 2 circuits, main circuit mult4x4
module mult4x4 (
  input  [3:0] A,
  input  [3:0] B,
  output [7:0] R
);

  wire [7:0] adder_1_r, adder_2_r, and_1_out, and_2_out, and_3_out, and_4_out;

  // Probe on A
  // Probe on B
  assign and_1_out = {4'b0000, A} & {8{B[0]}};  // AND_Gate and_1, 8 bits wide
  assign and_2_out = {3'b000, A, 1'b0} & {8{B[1]}};  // AND_Gate and_2, 8 bits wide
  assign and_3_out = {2'b00, A, 2'b00} & {8{B[2]}};  // AND_Gate and_3, 8 bits wide
  assign and_4_out = {1'b0, A, 3'b000} & {8{B[3]}};  // AND_Gate and_4, 8 bits wide
  adder adder_1 (.A(and_1_out), .B(and_2_out), .R(adder_1_r));
  adder adder_2 (.A(and_3_out), .B(and_4_out), .R(adder_2_r));
  adder adder_3 (.A(adder_1_r), .B(adder_2_r), .R(R));
  // Probe on R
endmodule

module adder (
  input  [7:0] A,
  input  [7:0] B,
  output [7:0] R
);

  wire [7:0] and_1_out, and_2_out, and_3_out;
  wire [7:1] xor_1_out;
  wire [7:7] xor_1_out_2;

  assign and_1_out = B & A;  // AND_Gate and_1, 8 bits wide
  assign and_2_out = A & {xor_1_out, 1'b0};  // AND_Gate and_2, 8 bits wide
  assign and_3_out = B & {xor_1_out, 1'b0};  // AND_Gate and_3, 8 bits wide
  assign {xor_1_out_2[7], xor_1_out} = and_3_out ^ and_2_out ^ and_1_out;  // XOR_Gate xor_1, 8 bits wide
  assign R = A ^ B ^ {xor_1_out, 1'b0};  // XOR_Gate xor_2, 8 bits wide
endmodule
