// Logisim project NSU-2023-T05L2e05.circ as structural Verilog: 3 circuits, main circuit bcd2
module bcd2 (
  input  Cin,
  input  [7:0] A,
  input  [7:0] B,
  output [7:0] R,
  output Cout
);

  wire bcd_add_1_cout;

  Hex_Digit_Display hex_digit_display_1 (.value(A[7:4]));  // open: dp
  Hex_Digit_Display hex_digit_display_2 (.value(B[7:4]));  // open: dp
  Hex_Digit_Display hex_digit_display_3 (.value({3'b000, Cin}));  // open: dp
  Hex_Digit_Display hex_digit_display_4 (.value(A[3:0]));  // open: dp
  Hex_Digit_Display hex_digit_display_5 (.value(B[3:0]));  // open: dp
  bcd_add bcd_add_1 (.Cin(Cin), .A(A[3:0]), .B(B[3:0]), .A_2(R[3:0]), .Cout(bcd_add_1_cout));
  bcd_add bcd_add_2 (.Cin(bcd_add_1_cout), .A(A[7:4]), .B(B[7:4]), .A_2(R[7:4]), .Cout(Cout));
  Hex_Digit_Display hex_digit_display_6 (.value({3'b000, Cout}));  // open: dp
  Hex_Digit_Display hex_digit_display_7 (.value(R[7:4]));  // open: dp
  Hex_Digit_Display hex_digit_display_8 (.value(R[3:0]));  // open: dp
endmodule

// BCD
module bcd_add (
  input  Cin,
  input  [3:0] A,
  input  [3:0] B,
  output [3:0] A_2,
  output Cout
);

  wire adder_1_cout, adder_2_cout, and_1_out, or_1_out;
  wire [3:0] adder_1_s, and_2_out;
  wire [3:3] or_2_out;

  // Probe on adder_1_s
  adder adder_1 (.Cin(Cin), .A(A), .B(B), .Cout(adder_1_cout), .S(adder_1_s));
  or or_1 (or_1_out, adder_1_s[1], adder_1_s[2]);
  and and_1 (and_1_out, or_1_out, adder_1_s[3]);
  or or_2 (or_2_out[3], adder_1_cout, and_1_out);
  adder adder_2 (.Cin(1'b0), .A(adder_1_s), .B(and_2_out), .Cout(adder_2_cout), .S(A_2));
  assign and_2_out = 4'b0110 & {4{or_2_out[3]}};  // AND_Gate and_2, 4 bits wide
  // Probe on A_2
  or or_3 (Cout, adder_1_cout, adder_2_cout);
endmodule

module adder (
  input  Cin,
  input  [3:0] A,
  input  [3:0] B,
  output Cout,
  output [3:0] S
);

  wire and_1_out, and_2_out, and_3_out, and_4_out, and_5_out, and_6_out, and_7_out, and_8_out, C0_out,
       C1_out, C2_out, xor_1_out, xor_2_out, xor_3_out, xor_4_out;

  xor xor_1 (xor_1_out, A[0], B[0]);
  and and_1 (and_1_out, A[0], B[0]);
  xor xor_2 (xor_2_out, A[1], B[1]);
  and and_2 (and_2_out, A[1], B[1]);
  xor xor_3 (xor_3_out, A[2], B[2]);
  and and_3 (and_3_out, A[2], B[2]);
  xor xor_4 (xor_4_out, A[3], B[3]);
  and and_4 (and_4_out, A[3], B[3]);
  xor S0 (S[0], xor_1_out, Cin);
  and and_5 (and_5_out, xor_1_out, Cin);
  xor S1 (S[1], xor_2_out, C0_out);
  and and_6 (and_6_out, xor_2_out, C0_out);
  xor S2 (S[2], xor_3_out, C1_out);
  and and_7 (and_7_out, xor_3_out, C1_out);
  xor S3 (S[3], xor_4_out, C2_out);
  and and_8 (and_8_out, xor_4_out, C2_out);
  or C0 (C0_out, and_5_out, and_1_out);
  or C1 (C1_out, and_6_out, and_2_out);
  or C2 (C2_out, and_7_out, and_3_out);
  or C3 (Cout, and_8_out, and_4_out);
endmodule
