// Logisim project NSU-2023-T05L2e02.circ as structural Verilog: 1 circuit, main circuit dec
module dec (
  input  [7:0] X,
  output [7:0] R,
  output Cout
);

  wire [6:0] xor_2_out;
  wire [7:0] and_1_out, and_2_out, and_3_out;

  assign and_1_out = X & {8{1'b1}};  // AND_Gate and_1, 8 bits wide
  assign and_2_out = {8{1'b1}} & {xor_2_out, 1'b0};  // AND_Gate and_2, 8 bits wide
  assign and_3_out = X & {xor_2_out, 1'b0};  // AND_Gate and_3, 8 bits wide
  assign R = X ^ {xor_2_out, 1'b0} ^ {8{1'b1}};  // XOR_Gate xor_1, 8 bits wide
  assign {Cout, xor_2_out} = and_1_out ^ and_2_out ^ and_3_out;  // XOR_Gate xor_2, 8 bits wide
endmodule
