// Logisim project NSU-2023-T05L2e04.circ as structural Verilog: 3 circuits, main circuit mult4x4
module mult4x4 (
  input  [3:0] A,
  input  [3:0] B,
  output [7:0] R
);

  wire not_1_out, not_2_out, not_3_out, not_4_out;
  wire [7:0] add_1_sum, add_2_sum, mux_1_output, mux_2_output, mux_3_output, mux_4_output;

  not not_1 (not_1_out, A[0]);
  not not_2 (not_2_out, A[1]);
  not not_3 (not_3_out, A[2]);
  not not_4 (not_4_out, A[3]);
  MUX mux_1 (.Input_0({4'b0000, B}), .sel(not_1_out), .Input_1({8{1'b0}}), .Output(mux_1_output));
  MUX mux_2 (.Input_0({3'b000, B, 1'b0}), .sel(not_2_out), .Input_1({8{1'b0}}), .Output(mux_2_output));
  MUX mux_3 (.Input_0({2'b00, B, 2'b00}), .sel(not_3_out), .Input_1({8{1'b0}}), .Output(mux_3_output));
  MUX mux_4 (.Input_0({1'b0, B, 3'b000}), .sel(not_4_out), .Input_1({8{1'b0}}), .Output(mux_4_output));
  add add_1 (.A(mux_1_output), .B(mux_2_output), .sum(add_1_sum));  // open: Cin, Cout
  add add_2 (.A(add_1_sum), .B(mux_3_output), .sum(add_2_sum));  // open: Cin, Cout
  add add_3 (.A(add_2_sum), .B(mux_4_output), .sum(R));  // open: Cin, Cout
endmodule

module add (
  input  [7:0] A,
  input  [7:0] B,
  input  Cin,
  output [7:0] sum,
  output Cout
);

  wire [6:0] or_1_out;
  wire [7:0] and_1_out, and_2_out, and_3_out;

  assign and_1_out = A & B;  // AND_Gate and_1, 8 bits wide
  assign and_2_out = B & {or_1_out, Cin};  // AND_Gate and_2, 8 bits wide
  assign and_3_out = A & {or_1_out, Cin};  // AND_Gate and_3, 8 bits wide
  assign {Cout, or_1_out} = and_1_out | and_2_out | and_3_out;  // OR_Gate or_1, 8 bits wide
  assign sum = A ^ {or_1_out, Cin} ^ B;  // XOR_Gate xor_1, 8 bits wide
  // also tied to GND on the sheet: Cin
endmodule

module MUX (
  input  [7:0] Input_0,
  input  sel,
  input  [7:0] Input_1,
  output [7:0] Output
);

  wire [7:0] and_1_out, and_2_out;
  wire [7:7] not_1_out;

  not not_1 (not_1_out[7], sel);
  assign and_1_out = Input_0 & {8{not_1_out[7]}};  // AND_Gate and_1, 8 bits wide
  assign and_2_out = {8{sel}} & Input_1;  // AND_Gate and_2, 8 bits wide
  assign Output = and_1_out | and_2_out;  // OR_Gate or_1, 8 bits wide
endmodule
