// Logisim project NSU-2023-T05L3e01.circ as structural Verilog: 1 circuit, main circuit ALU
module ALU (
  input  Cin,
  input  [7:0] A,
  input  [7:0] B,
  input  [1:0] instr,
  output [7:0] R,
  output Cout,
  output V
);

  wire xor_2_out, xor_4_out;
  wire [7:0] and_1_out, and_2_out, and_3_out, and_4_out, and_5_out, and_6_out, and_7_out, negator_1_out,
       or_1_out, xor_1_out, xor_3_out;
  wire [7:1] or_2_out, or_3_out;
  wire [7:7] or_2_out_2, or_3_out_2;

  assign and_1_out = A & B;  // AND_Gate and_1, 8 bits wide
  assign or_1_out = A | B;  // OR_Gate or_1, 8 bits wide
  assign xor_1_out = A ^ {or_2_out, Cin} ^ B;  // XOR_Gate xor_1, 8 bits wide
  assign and_2_out = B & A;  // AND_Gate and_2, 8 bits wide
  assign {or_2_out_2[7], or_2_out} = and_2_out | and_3_out | and_4_out;  // OR_Gate or_2, 8 bits wide
  assign and_3_out = B & {or_2_out, Cin};  // AND_Gate and_3, 8 bits wide
  assign and_4_out = A & {or_2_out, Cin};  // AND_Gate and_4, 8 bits wide
  xor xor_2 (xor_2_out, or_2_out[7], or_2_out_2[7]);
  Negator negator_1 (.in(B), .out(negator_1_out));
  assign and_5_out = negator_1_out & A;  // AND_Gate and_5, 8 bits wide
  assign and_6_out = negator_1_out & {or_3_out, Cin};  // AND_Gate and_6, 8 bits wide
  assign and_7_out = A & {or_3_out, Cin};  // AND_Gate and_7, 8 bits wide
  assign xor_3_out = A ^ {or_3_out, Cin} ^ negator_1_out;  // XOR_Gate xor_3, 8 bits wide
  assign {or_3_out_2[7], or_3_out} = and_5_out | and_6_out | and_7_out;  // OR_Gate or_3, 8 bits wide
  xor xor_4 (xor_4_out, or_3_out[7], or_3_out_2[7]);
  Multiplexer #(.select(2), .disabled(0)) multiplexer_1 (
    .in0(1'b0), .in1(1'b0), .in2(or_2_out_2[7]), .in3(or_3_out_2[7]), .out(Cout), .sel(instr));  // open: en
  Multiplexer #(.select(2), .disabled(0)) multiplexer_2 (
    .in0(1'b0), .in1(1'b0), .in2(xor_2_out), .in3(xor_4_out), .out(V), .sel(instr));  // open: en
  Multiplexer #(.select(2), .width(8), .disabled(0)) multiplexer_3 (
    .in0(and_1_out), .in1(or_1_out), .in2(xor_1_out), .in3(xor_3_out), .out(R), .sel(instr));  // open: en

  // Notes on the sheet:
  //   00: and
  //   01: or
  //   10: add
  //   11: sub
endmodule
