// Logisim project NSU-2023-T06L1e01.circ as structural Verilog: 1 circuit, main circuit fib32
module fib32 (
  input  clock,
  output [31:0] a,
  output [5:0] k,
  output stop
);

  wire comparator_1_lt, comparator_2_lt;
  wire [5:0] counter_1_q;
  wire [31:0] buffer_1_out, buffer_2_out, multiplexer_1_out, multiplexer_2_out, register_1_q, register_2_q;

  Comparator #(.width(32), .mode("unsigned")) comparator_1 (.a(a), .b(32'h1), .lt(comparator_1_lt));  // open: gt, eq
  Multiplexer #(.width(32)) multiplexer_1 (
    .in0(a), .in1(32'h1), .out(multiplexer_1_out), .sel(comparator_1_lt));  // open: en
  Register #(.width(32)) register_1 (.D(multiplexer_1_out), .Q(register_1_q), .clk(clock));  // open: en, clr
  // Probe on register_1_q
  assign buffer_1_out = buffer_2_out;  // Buffer buffer_1, 32 bits wide
  assign buffer_2_out = register_1_q;  // Buffer buffer_2, 32 bits wide
  Comparator #(.width(32), .mode("unsigned")) comparator_2 (
    .a(buffer_1_out), .b(32'h1), .lt(comparator_2_lt));  // open: gt, eq
  Multiplexer #(.width(32)) multiplexer_2 (
    .in0(buffer_1_out), .in1(32'h1), .out(multiplexer_2_out), .sel(comparator_2_lt));  // open: en
  // Probe on register_2_q
  Register #(.width(32)) register_2 (.D(multiplexer_2_out), .Q(register_2_q), .clk(clock));  // open: en, clr
  Counter #(.width(6), .max('h3f), .ongoal("stay")) counter_1 (
    .Q(counter_1_q), .clk(clock));  // open: load, D, count, carry, clr
  Adder #(.width(32)) adder_1 (.a(register_1_q), .b(register_2_q), .out(a), .cout(stop));  // open: cin
  Adder #(.width(6)) adder_2 (.a(counter_1_q), .b(6'b000001), .out(k));  // open: cin, cout
  // Probe on a

  // Other names for the same wires on the sheet: clck = clock
endmodule
